// Logisim project part1.circ as structural Verilog
module _4bitcounter (
  input  inc,
  input  rst,
  output [3:0] \output 
);

  wire and_1_out, and_2_out, and_3_out, and_4_out, and_5_out, and_6_out, clk_out, not_1_out, not_2_out,
       xor_1_out, xor_2_out, xor_3_out;

  Clock clk (.out(clk_out));
  and and_1 (and_1_out, \output [0], \output [1]);
  not not_1 (not_1_out, rst);
  not not_2 (not_2_out, \output [0]);
  xor xor_1 (xor_1_out, \output [0], \output [1]);
  xor xor_2 (xor_2_out, and_1_out, \output [2]);
  and and_2 (and_2_out, and_1_out, \output [2]);
  xor xor_3 (xor_3_out, and_2_out, \output [3]);
  and and_3 (and_3_out, not_2_out, inc, not_1_out);
  and and_4 (and_4_out, xor_1_out, inc, not_1_out);
  and and_5 (and_5_out, xor_2_out, inc, not_1_out);
  and and_6 (and_6_out, xor_3_out, inc, not_1_out);
  D_Flip_Flop d_ff_1 (.clk(clk_out), .D(and_3_out), .Q(\output [0]));  // open: Qn, preset, en, reset
  D_Flip_Flop d_ff_2 (.clk(clk_out), .D(and_4_out), .Q(\output [1]));  // open: Qn, preset, en, reset
  D_Flip_Flop d_ff_3 (.clk(clk_out), .D(and_5_out), .Q(\output [2]));  // open: Qn, preset, en, reset
  D_Flip_Flop d_ff_4 (.clk(clk_out), .D(and_6_out), .Q(\output [3]));  // open: Qn, preset, en, reset

  // Other names for the same wires on the sheet: b1 = \output [0]; b2 = \output [1]; b3 = \output [2];
  //   b4 = \output [3]
endmodule

module main (
);

  wire rst_out;
  wire [3:0] n4bitcounter_1_output;

  Button rst (.out(rst_out));
  Hex_Digit_Display hex_digit_display_1 (.value(n4bitcounter_1_output));  // open: dp
  _4bitcounter u_4bitcounter_1 (.inc(1'b1), .rst(rst_out), .\output (n4bitcounter_1_output));
endmodule
